// Logisim project guia7.circ as structural Verilog: 1 circuit, main circuit main
module main (
  output [7:0] out_1,
  output [7:0] out_2
);

  wire clock_1_out;

  Adder adder_1 (.a(8'h1), .b(out_2), .out(out_1));  // open: cin, cout
  Clock clock_1 (.out(clock_1_out));
  Register register_1 (.D(out_1), .Q(out_2), .clk(clock_1_out));  // open: en, clr
endmodule
