// Logisim project guia8ejemplo.circ as structural Verilog: 1 circuit, main circuit guia8ejemplo
module guia8ejemplo (
  input  X,
  input  Y,
  input  Z,
  output Q1,
  output Q2
);

  wire and_1_out, and_2_out, and_3_out, and_4_out, and_5_out, not_1_out, not_2_out, not_3_out, not_4_out,
       not_5_out;

  not not_1 (not_1_out, X);
  not not_2 (not_2_out, Z);
  not not_3 (not_3_out, Z);
  not not_4 (not_4_out, Y);
  not not_5 (not_5_out, Z);
  and and_1 (and_1_out, not_1_out, not_2_out);
  and and_2 (and_2_out, Y, not_3_out);
  and and_3 (and_3_out, X, Z);
  and and_4 (and_4_out, not_4_out, Z);
  and and_5 (and_5_out, Y, not_5_out);
  or or_1 (Q1, and_1_out, and_2_out, and_3_out);
  or or_2 (Q2, and_4_out, and_5_out);
endmodule
