// Logisim project guia8ejercicio1.circ as structural Verilog: 1 circuit, main circuit guia8ejercicio1
module guia8ejercicio1 (
  input  X,
  input  Y,
  input  Z,
  output F
);

  wire and_1_out, and_2_out, not_1_out;

  not not_1 (not_1_out, X);
  and and_1 (and_1_out, not_1_out, Y);
  and and_2 (and_2_out, X, Z);
  or or_1 (F, and_1_out, and_2_out);
endmodule
