// Logisim project guia8ejercicio2.circ as structural Verilog: 1 circuit, main circuit guia8ejercicio2
module guia8ejercicio2 (
  input  A,
  input  B,
  input  C,
  input  D,
  output X
);

  wire and_1_out, and_2_out, and_3_out, and_4_out, and_5_out, not_1_out, not_2_out, not_3_out, not_4_out,
       not_5_out, not_6_out, not_7_out, not_8_out, not_9_out, not_10_out, not_11_out, not_12_out, not_13_out,
       not_14_out;

  not not_1 (not_1_out, A);
  not not_2 (not_2_out, B);
  not not_3 (not_3_out, C);
  not not_4 (not_4_out, D);
  not not_5 (not_5_out, A);
  not not_6 (not_6_out, B);
  not not_7 (not_7_out, C);
  not not_8 (not_8_out, A);
  not not_9 (not_9_out, D);
  not not_10 (not_10_out, B);
  not not_11 (not_11_out, D);
  not not_12 (not_12_out, A);
  not not_13 (not_13_out, C);
  not not_14 (not_14_out, D);
  and and_1 (and_1_out, not_1_out, not_2_out, not_3_out, not_4_out);
  and and_2 (and_2_out, not_5_out, not_6_out, not_7_out, D);
  and and_3 (and_3_out, not_8_out, B, C, not_9_out);
  and and_4 (and_4_out, A, not_10_out, C, not_11_out);
  and and_5 (and_5_out, not_12_out, B, not_13_out, not_14_out);
  or or_1 (X, and_1_out, and_2_out, and_3_out, and_4_out, and_5_out);
endmodule
