// Logisim project guia9ejemplo.circ as structural Verilog: 2 circuits, main circuit main
module main (
);

  subcircuito subcircuito_1 ();  // open: in_1, in_2, in_3, out_4, out_5
endmodule

module subcircuito (
  input  in_1,
  input  in_2,
  input  in_3,
  output out_4,
  output out_5
);

  D_Flip_Flop d_ff_1 (.clk(in_1), .D(in_2), .Q(out_4));  // open: Qn, preset, en, reset
  D_Flip_Flop d_ff_2 (.clk(in_1), .D(in_3), .Q(out_5));  // open: Qn, preset, en, reset
endmodule
